# Fritzing sketch Aircon (saved by Fritzing 1.0.6)
circuit board: 8.46667cm x 5.64444cm
stripboards: 1

parts:
  R1 = Resistor [tolerance=±5% power=0.25W resistance=22k package=THT]
  R2 = Resistor [tolerance=±5% power=0.25W resistance=4.7k package=THT]
  R3 = Resistor [tolerance=±5% power=0.25W resistance=1k package=THT]
  J2 = JST-B3B-XH-A [part_number=B3B-XH-A package=THT]
  A2 = MCP4725 [part_number=MCP4725]
  A1 = Esp32-c3 super mini [part_number=ESP32-C3]
  U1 = HW-133 DC-DC Module [part_number=HW-133]
  C1 = Electrolytic Capacitor [capacitance=1mF voltage=25V package="100 mil [THT, electrolytic]"]
  D1 = Schottky Diode [part_number=1N5817 package="300 mil [THT]"]
  Q1 = NPN-Transistor [package="TO92 [THT]"]

nets:
  N1: R1.Pin_0, A2.pin1
  N2: R1.Pin_1, Q1.B
  N3: R2.Pin_0, J2.pin1, D1.anode
  N4: R2.Pin_1, R3.Pin_0, A1.Pin_13
  GND: R3.Pin_1, J2.pin2, A2.pin2, A1.Pin_15, U1.GND_IN, U1.GND_IN_(2), U1.GND_OUT, U1.GND_OUT_(2), C1.-, Q1.E
  N5: J2.pin3, Q1.C
  N6: A2.pin3, A1.Pin_12
  N7: A2.pin4, A1.Pin_6
  N8: A2.pin5, A1.Pin_16, U1.VCC_OUT, U1.VCC_OUT_(2)
  N9: U1.VCC_IN, U1.VCC_IN_(2), C1.+, D1.cathode

notes:
  3: Key-A
  2: COM
  1: POWER-C
  16: 5V
  15: GND
  13: GPIO4
  12: GPIO3/SCL
  10: GPIO10/SDA

custom parts:
  MCP4725: The MCP4725 is an I2C controlled Digital-to-Analog converter (DAC) based on Fritzing Part-o-matic
  Esp32-c3 super mini: ESP32-C3 Development Board ESP32 SuperMini Development Board ESP32 Development Board WiFi Bluetooth.
  HW-133 DC-DC Module: HW-133 DC-DC Module Adapter with variable input/output Adapted from DSUN-DC by Bluewalk
